// Logisim project Cache.circ as structural Verilog: 10 circuits, main circuit main
module main (
  input  EnableTestHalting,
  output [9:0] CorrectCounter,
  output [9:0] HitCounter,
  output [9:0] MissCounter,
  output [9:0] TestNumber,
  output [7:0] ByteRead,
  output [7:0] CorrectByteRead,
  output Halt
);

  wire and_3_out, and_4_out, and_5_out, CLK, CmdIsRead, Correct, CpuRead, CpuWrite, DidContain, HaltTesting,
       MaxItersReached, MemRead, MemWrite, not_1_out, not_2_out, not_4_out, NotDoneTesting, Ok2Count,
       or_1_out, Ready;
  wire [7:0] CpuWriteValue, MemAddress;
  wire [9:0] CpuAddress;
  wire [31:0] Line2Mem, LineFromMem;

  not not_1 (not_1_out, Ready);
  Clock clock_1 (.out(CLK));
  or or_1 (or_1_out, MaxItersReached, Ready);
  Counter #(.width(4), .max('h9)) MaxClocks (
    .load(Ready), .D(4'b0001), .count(not_1_out), .carry(MaxItersReached), .clk(CLK));  // open: Q, clr
  and and_1 (HaltTesting, EnableTestHalting, CmdIsRead, not_2_out);
  not not_2 (not_2_out, Correct);
  not not_3 (NotDoneTesting, Halt);
  Inputs inputs_1 (
    .HaltTesting(HaltTesting), .Ready(or_1_out), .CLK(CLK), .Done(Halt), .Read(CpuRead), .Write(CpuWrite),
    .Address(CpuAddress), .Value(CpuWriteValue), .TestNumber(TestNumber));
  Cache cache_1 (
    .CpuAddress(CpuAddress), .CpuRead(CpuRead), .CpuWrite(CpuWrite), .CpuWriteValue(CpuWriteValue),
    .CLK(CLK), .Ready(Ready), .DidContain(DidContain), .ByteRead(ByteRead), .MemAddress(MemAddress),
    .MemRead(MemRead), .MemWrite(MemWrite), .LineFromMem(LineFromMem), .Line2Mem(Line2Mem));
  // Probe on CpuRead
  // Probe on CpuWrite
  // Probe on CpuAddress
  // Probe on CpuWriteValue
  // Probe on TestNumber
  // Probe on CorrectByteRead
  // Probe on Correct
  // Probe on Ready
  // Probe on DidContain
  // Probe on ByteRead
  // Probe on MemAddress
  // Probe on MemRead
  // Probe on MemWrite
  // Probe on HitCounter
  // Probe on LineFromMem
  // Probe on Line2Mem
  not not_4 (not_4_out, HaltTesting);
  RAM #(.dataWidth(32), .bus("separate")) ram_1 (
    .addr(MemAddress), .din(Line2Mem), .data(LineFromMem), .str(MemWrite), .clk(CLK), .ld(MemRead));  // open: sel, clr
  and and_2 (Ok2Count, Ready, not_4_out, NotDoneTesting);
  and and_3 (and_3_out, Correct, Ok2Count);
  and and_4 (and_4_out, DidContain, Ok2Count);
  and and_5 (and_5_out, MemRead, NotDoneTesting);
  Checker checker_1 (
    .TestNumber(TestNumber), .YourByteRead(ByteRead), .CmdIsRead(CmdIsRead),
    .CorrectByteRead(CorrectByteRead), .Correct(Correct));
  Counter #(.width(10), .max('h3ff)) u_CorrectCounter (
    .count(and_3_out), .Q(CorrectCounter), .clk(CLK));  // open: load, D, carry, clr
  Counter #(.width(10), .max('h3ff)) u_HitCounter (
    .count(and_4_out), .Q(HitCounter), .clk(CLK));  // open: load, D, carry, clr
  Counter #(.width(10), .max('h3ff)) u_MissCounter (
    .count(and_5_out), .Q(MissCounter), .clk(CLK));  // open: load, D, carry, clr
  // Probe on CorrectCounter
  // Probe on HitCounter
  // Probe on MissCounter

  // Other names for the same wires on the sheet: DoneTesting = Halt

  // Notes on the sheet:
  //   Your Answer Inside Here
endmodule

module Cache (
  input  [9:0] CpuAddress,
  input  CpuRead,
  input  CpuWrite,
  input  [31:0] LineFromMem,
  input  [7:0] CpuWriteValue,
  input  CLK,
  output Ready,
  output DidContain,
  output [7:0] ByteRead,
  output [7:0] MemAddress,
  output MemRead,
  output MemWrite,
  output [31:0] Line2Mem
);

  wire CpuRead_t, CpuWrite_t, Enable0, Enable1, Evict, InCache, InCache0, InCache1, Init, IsDirty, IsDirty0,
       IsDirty1, UpdateAges, WriteBlock, WriteByte;
  wire [1:0] multiplexer_6_out;
  wire [6:0] Tag0, Tag1;
  wire [7:0] ByteOut0, ByteOut1, ByteRead_t, CpuWriteValue_t;
  wire [9:0] CpuAddress_t;
  wire [9:2] Addr2WriteTo;
  wire [31:0] BlockOut0, BlockOut1;

  Register #(.width(10), .trigger("falling")) CPUAddr (
    .D(CpuAddress), .en(Ready), .Q({CpuAddress_t[9:3], Addr2WriteTo[2], CpuAddress_t[1:0]}), .clk(CLK));  // open: clr
  Register #(.trigger("falling")) CPUWriteVal (
    .D(CpuWriteValue), .en(Ready), .Q(CpuWriteValue_t), .clk(CLK));  // open: clr
  // Probe on {CpuAddress_t[9:3], Addr2WriteTo[2], CpuAddress_t[1:0]}
  Register #(.width(1), .trigger("falling")) CPUAddr_2 (
    .D(CpuRead), .en(Ready), .Q(CpuRead_t), .clk(CLK));  // open: clr
  Register #(.width(1), .trigger("falling")) CPUAddr_3 (
    .D(CpuWrite), .en(Ready), .Q(CpuWrite_t), .clk(CLK));  // open: clr
  // Probe on CpuWriteValue_t
  Demultiplexer #(.enable("false")) demultiplexer_1 (.out0(Enable0), .out1(Enable1), .in(1'b1), .sel(Addr2WriteTo[2]));
  FSM fsm_1 (
    .InCache(InCache), .CPURead(CpuRead_t), .CPUWrite(CpuWrite_t), .IsDirty(IsDirty), .MemRead(MemRead),
    .MemWrite(MemWrite), .Evict(Evict), .UpdateAges(UpdateAges), .WriteBlock(WriteBlock),
    .WriteByte(WriteByte), .Init(Init), .Ready(Ready), .InCache_2(DidContain));
  Set set_1 (
    .Init(Init), .Enable(Enable0), .UpdateAges(UpdateAges), .EvictBlock(Evict),
    .Addr({CpuAddress_t[9:3], Addr2WriteTo[2], CpuAddress_t[1:0]}), .WriteByte(WriteByte),
    .ByteToWrite(CpuWriteValue_t), .WriteBlock(WriteBlock), .BlockToWrite(LineFromMem), .Clock(CLK),
    .InCache(InCache0), .IsDirty(IsDirty0), .ByteOut(ByteOut0), .BlockOut(BlockOut0), .TagOut(Tag0));
  Multiplexer #(.enable("false")) multiplexer_1 (.in0(InCache0), .in1(InCache1), .out(InCache), .sel(Addr2WriteTo[2]));
  Multiplexer #(.enable("false")) multiplexer_2 (.in0(IsDirty0), .in1(IsDirty1), .out(IsDirty), .sel(Addr2WriteTo[2]));
  Multiplexer #(.width(8), .enable("false")) multiplexer_3 (
    .in0(ByteOut0), .in1(ByteOut1), .out(ByteRead_t), .sel(Addr2WriteTo[2]));
  Multiplexer #(.width(32), .enable("false")) multiplexer_4 (
    .in0(BlockOut0), .in1(BlockOut1), .out(Line2Mem), .sel(Addr2WriteTo[2]));
  Multiplexer #(.width(7), .enable("false")) multiplexer_5 (
    .in0(Tag0), .in1(Tag1), .out(Addr2WriteTo[9:3]), .sel(Addr2WriteTo[2]));
  Multiplexer #(.width(10), .enable("false")) multiplexer_6 (
    .in0({CpuAddress_t[9:3], Addr2WriteTo[2], CpuAddress_t[1:0]}), .in1({Addr2WriteTo, 2'b00}),
    .out({MemAddress, multiplexer_6_out}), .sel(MemWrite));
  // Probe on MemAddress
  Set set_2 (
    .Init(Init), .Enable(Enable1), .UpdateAges(UpdateAges), .EvictBlock(Evict),
    .Addr({CpuAddress_t[9:3], Addr2WriteTo[2], CpuAddress_t[1:0]}), .WriteByte(WriteByte),
    .ByteToWrite(CpuWriteValue_t), .WriteBlock(WriteBlock), .BlockToWrite(LineFromMem), .Clock(CLK),
    .InCache(InCache1), .IsDirty(IsDirty1), .ByteOut(ByteOut1), .BlockOut(BlockOut1), .TagOut(Tag1));
  // Probe on Tag1
  Register #(.trigger("falling")) CPUAddr_4 (.D(ByteRead_t), .Q(ByteRead), .clk(CLK));  // open: en, clr

  // Other names for the same wires on the sheet: MemAddr[7:0] = MemAddress; CpuAddress_t[2] = Addr2WriteTo[2];
  //   Set = Addr2WriteTo[2]; Index[1:0] = CpuAddress_t[1:0]; Tag[6:0] = CpuAddress_t[9:3]

  // Notes on the sheet:
  //   Address Bits = 10
  //   Line Size = 4
  //   W = 3
  //   Group Members:
  //   Num Sets = 2
  //   Matthew Donnelly (SID: 914636887)
  //   Shayan Shahbazi (SID: 915255597)
  //   C =4*3*2 = 24bytes
  //   Tag bits = 7
endmodule

module Inputs (
  input  HaltTesting,
  input  Ready,
  input  CLK,
  output Done,
  output Read,
  output Write,
  output [9:0] Address,
  output [7:0] Value,
  output [9:0] TestNumber
);

  wire and_1_out, not_1_out, not_2_out;

  not not_1 (not_1_out, HaltTesting);
  not not_2 (not_2_out, Done);
  Counter #(.width(10), .max('h3ff), .ongoal("stay")) u_TestNumber (
    .count(and_1_out), .Q(TestNumber), .clk(CLK));  // open: load, D, carry, clr
  and and_1 (and_1_out, not_1_out, Ready, not_2_out);
  ROM #(.addrWidth(10), .dataWidth(21)) rom_1 (
    .addr(TestNumber), .data({Done, Read, Write, Address, Value}));  // open: sel

  // Notes on the sheet:
  //   contents of rom_1 (hex, n*v repeats v):
  //   80882 83fe6 4306b 83e0e 43701 42275 8280f 80304 41bd8 84371 43f77 41d70 4250b 44733 8253d 440d8
  //   82691 440c9 83d7c 43558 446bf 83837 842c9 43e0f 4059d 41556 80166 833b0 43a89 83142 8361c 42e66
  //   43eb6 42c00 43a0e 8165c 84682 8092a 83907 41f89 817b0 40855 82056 425e8 43ff2 8039f 42bd7 82137
  //   4416b 40273 8324a 814e4 44570 41c0f 429da 82640 8069c 8099e 414d5 41004 81beb 84113 419b1 81add
  //   83f35 425ff 829cd 40250 82945 4366d 40cc2 444f8 80814 81156 8446d 42a82 42bae 82578 41135 405d0
  //   8304b 82b3a 40972 822ba 4443a 42337 82506 80bd3 80560 83552 83955 81434 43096 43da1 81aa2 80305
  //   428e6 428cc 808a2 40e80 845f0 4215d 82765 82e29 40be5 82b74 42715 417a2 41fab 8452f 81c0a 83325
  //   44624 80205 42dfc 41333 40958 81348 42736 41069 84510 44669 826dd 8067e 408e4 44680 444e8 832ad
  //   821f8 83509 82d46 81184 432cd 80b77 4005a 440e0 81ea0 43d73 42b8c 80624 41468 42699 415ed 80fc1 0
  //   100000
endmodule

module Checker (
  input  [9:0] TestNumber,
  input  [7:0] YourByteRead,
  output CmdIsRead,
  output [7:0] CorrectByteRead,
  output Correct
);

  wire comparator_1_eq;
  wire [9:0] subtractor_1_out;

  // Probe on TestNumber
  Subtractor #(.width(10)) subtractor_1 (.a(TestNumber), .b(10'h1), .out(subtractor_1_out));  // open: bin, bout
  ROM #(.addrWidth(10), .dataWidth(9)) rom_1 (
    .addr(subtractor_1_out), .data({CmdIsRead, CorrectByteRead}));  // open: sel
  // Probe on CorrectByteRead
  Comparator #(.mode("unsigned")) comparator_1 (
    .a(YourByteRead), .b(CorrectByteRead), .eq(comparator_1_eq));  // open: gt, lt
  and and_1 (Correct, comparator_1_eq, CmdIsRead);

  // Other names for the same wires on the sheet: Test_Number[9:0] = TestNumber

  // Notes on the sheet:
  //   Read Solutions
  //   contents of rom_1 (hex, n*v repeats v):
  //   1a3 1dc 6b 125 1 75 1dc 1c3 d8 1ab 77 70 b 33 10b d8 1c3 c9 174 58 bf 153 199 f 9d 56 1bb 13b 89 16c
  //   180 66 b6 0 e 107 1bf 1d8 167 89 118 55 1a2 e8 f2 1c3 d7 142 6b 73 1ab 18c 70 f da 1c3 14c 1d8 d5 4
  //   1d8 16b b1 1f4 1f2 ff 1da 50 1da 6d c2 f8 155 1c6 1f8 82 ae 1ff 35 d0 16b 1ae 72 175 3a 37 1ff 173
  //   1d0 158 167 1d5 96 a1 1f4 1c3 e6 cc 155 80 170 5d 1e6 166 e5 1ae 15 a2 ab 170 10f 13b 24 150 fc 33
  //   58 133 36 69 170 69 1c3 14c e4 80 e8 1ab 15d 158 1fc 135 cd 1e5 5a e0 104 73 8c 14c 68 99 ed 1a6
endmodule

module Set (
  input  Init,
  input  Enable,
  input  UpdateAges,
  input  EvictBlock,
  input  [9:0] Addr,
  input  WriteByte,
  input  [7:0] ByteToWrite,
  input  WriteBlock,
  input  [31:0] BlockToWrite,
  input  Clock,
  output InCache,
  output IsDirty,
  output [7:0] ByteOut,
  output [31:0] BlockOut,
  output [6:0] TagOut
);

  wire and_1_out, and_2_out, and_3_out, and_4_out, and_5_out, and_6_out, B0Enabled, B1Enabled, B2Enabled,
       comparator_1_eq, comparator_2_eq, comparator_3_eq, Dirty0, Dirty1, Dirty2, InBlock0, InBlock1,
       InBlock2;
  wire [1:0] AgeAccessed, bitfinder_1_index, bitfinder_2_index, bitfinder_3_index, Block0Age, Block1Age,
       Block2Age;
  wire [6:0] Block0Tag, Block1Tag, Block2Tag;
  wire [31:0] BlockOut0, BlockOut1, BlockOut2, or_4_out;

  BitFinder #(.width(3)) bitfinder_1 (.in({InBlock2, InBlock1, InBlock0}), .index(bitfinder_1_index));  // open: found
  Multiplexer #(.select(2), .width(2), .enable("false")) multiplexer_1 (
    .in0(Block0Age), .in1(Block1Age), .in2(Block2Age), .out(AgeAccessed), .sel(bitfinder_1_index));  // open: in3
  Comparator #(.width(2), .mode("unsigned")) comparator_1 (
    .a(Block0Age), .b(2'b10), .eq(comparator_1_eq));  // open: gt, lt
  Comparator #(.width(2), .mode("unsigned")) comparator_2 (
    .a(Block1Age), .b(2'b10), .eq(comparator_2_eq));  // open: gt, lt
  Comparator #(.width(2), .mode("unsigned")) comparator_3 (
    .a(Block2Age), .b(2'b10), .eq(comparator_3_eq));  // open: gt, lt
  and and_1 (and_1_out, InBlock0, Enable);
  and and_2 (and_2_out, EvictBlock, Enable, comparator_1_eq);
  and and_3 (and_3_out, InBlock1, Enable);
  and and_4 (and_4_out, EvictBlock, Enable, comparator_2_eq);
  and and_5 (and_5_out, InBlock2, Enable);
  and and_6 (and_6_out, EvictBlock, Enable, comparator_3_eq);
  or or_1 (B0Enabled, and_1_out, and_2_out);
  or or_2 (B1Enabled, and_3_out, and_4_out);
  or or_3 (B2Enabled, and_5_out, and_6_out);
  // Probe on InBlock0
  Block2 block2_1 (
    .Enable(B0Enabled), .Init(Init), .StartAge(2'b00), .Addr(Addr), .WriteByte(WriteByte),
    .ByteToWrite(ByteToWrite), .WriteBlock(WriteBlock), .BlockToWrite(BlockToWrite), .UpdateAge(UpdateAges),
    .AgeAccessed(AgeAccessed), .Clock(Clock), .InBlock(InBlock0), .IsDirty(Dirty0), .BlockData(BlockOut0),
    .BlockAge(Block0Age), .EvictedBlockTag(Block0Tag));
  // Probe on Block0Age
  // Probe on InBlock1
  Block2 block2_2 (
    .Enable(B1Enabled), .Init(Init), .StartAge(2'b01), .Addr(Addr), .WriteByte(WriteByte),
    .ByteToWrite(ByteToWrite), .WriteBlock(WriteBlock), .BlockToWrite(BlockToWrite), .UpdateAge(UpdateAges),
    .AgeAccessed(AgeAccessed), .Clock(Clock), .InBlock(InBlock1), .IsDirty(Dirty1), .BlockData(BlockOut1),
    .BlockAge(Block1Age), .EvictedBlockTag(Block1Tag));
  // Probe on Block1Age
  // Probe on InBlock2
  Block2 block2_3 (
    .Enable(B2Enabled), .Init(Init), .StartAge(2'b10), .Addr(Addr), .WriteByte(WriteByte),
    .ByteToWrite(ByteToWrite), .WriteBlock(WriteBlock), .BlockToWrite(BlockToWrite), .UpdateAge(UpdateAges),
    .AgeAccessed(AgeAccessed), .Clock(Clock), .InBlock(InBlock2), .IsDirty(Dirty2), .BlockData(BlockOut2),
    .BlockAge(Block2Age), .EvictedBlockTag(Block2Tag));
  // Probe on Block2Age
  // Probe on Dirty1
  // Probe on Dirty2
  // Probe on Dirty0
  // Probe on BlockOut1
  // Probe on BlockOut2
  // Probe on BlockOut0
  assign or_4_out = BlockOut0 | BlockOut1 | BlockOut2;  // OR_Gate or_4, 32 bits wide
  BitFinder #(.width(3)) bitfinder_2 (
    .in({B2Enabled, B1Enabled, B0Enabled}), .index(bitfinder_2_index));  // open: found
  BitFinder #(.width(3)) bitfinder_3 (
    .in({B2Enabled, B1Enabled, B0Enabled}), .index(bitfinder_3_index));  // open: found
  // Probe on InCache
  or or_5 (InCache, InBlock0, InBlock1, InBlock2);
  // Probe on IsDirty
  Multiplexer #(.select(2), .enable("false")) multiplexer_2 (
    .in0(Dirty0), .in1(Dirty1), .in2(Dirty2), .out(IsDirty), .sel(bitfinder_2_index));  // open: in3
  Multiplexer #(.select(2), .width(8), .enable("false")) multiplexer_3 (
    .in0(or_4_out[7:0]), .in1(or_4_out[15:8]), .in2(or_4_out[23:16]), .in3(or_4_out[31:24]), .out(ByteOut),
    .sel(Addr[1:0]));
  assign BlockOut = BlockOut0 | BlockOut1 | BlockOut2;  // OR_Gate or_6, 32 bits wide
  Multiplexer #(.select(2), .width(7), .enable("false")) multiplexer_4 (
    .in0(Block0Tag), .in1(Block1Tag), .in2(Block2Tag), .out(TagOut), .sel(bitfinder_3_index));  // open: in3

  // Other names for the same wires on the sheet: Index[1:0] = Addr[1:0]; Set = Addr[2]; Tag[6:0] = Addr[9:3]
endmodule

module FSM (
  input  InCache,
  input  CPURead,
  input  CPUWrite,
  input  IsDirty,
  output MemRead,
  output MemWrite,
  output Evict,
  output UpdateAges,
  output WriteBlock,
  output WriteByte,
  output Init,
  output Ready,
  output InCache_2
);

  wire CLK;
  wire [2:0] CurrState, NextState;

  Clock clock_1 (.out(CLK));
  OutputEquation Output (
    .S2(CurrState[2]), .S1(CurrState[1]), .S0(CurrState[0]), .Clock(CLK), .S2_2(NextState[2]),
    .S1_2(NextState[1]), .S0_2(NextState[0]), .MemRead(MemRead), .MemWrite(MemWrite), .Evict(Evict),
    .UpdateAge(UpdateAges), .WriteBlock(WriteBlock), .WriteByte(WriteByte), .Init(Init), .Ready(Ready),
    .InCache(InCache_2));
  Next_State next_state_1 (
    .S2(CurrState[2]), .S1(CurrState[1]), .S0(CurrState[0]), .C(InCache), .R(CPURead), .W(CPUWrite),
    .D(IsDirty), .S2P(NextState[2]), .S1P(NextState[1]), .S0P(NextState[0]));
  // Probe on CurrState
  // Probe on NextState
  Register #(.width(3)) State (.D(NextState), .Q(CurrState), .clk(CLK));  // open: en, clr

  // Other names for the same wires on the sheet: C = InCache; D = IsDirty; R = CPURead; W = CPUWrite
endmodule

module Block2 (
  input  Enable,
  input  Init,
  input  [1:0] StartAge,
  input  [9:0] Addr,
  input  WriteByte,
  input  [7:0] ByteToWrite,
  input  WriteBlock,
  input  [31:0] BlockToWrite,
  input  UpdateAge,
  input  [1:0] AgeAccessed,
  input  Clock,
  output InBlock,
  output IsDirty,
  output [31:0] BlockData,
  output [1:0] BlockAge,
  output [6:0] EvictedBlockTag
);

  wire Byte0, Byte1, Byte2, Byte3, comparator_2_eq, IsValid, or_1_out, or_2_out, or_3_out, or_4_out,
       or_5_out, or_6_out, WriteBlock_t, WriteByte_t;
  wire [1:0] adder_1_out, comparator_1_eq, multiplexer_3_out, multiplexer_4_out;
  wire [7:0] controlled_buffer_1_out, controlled_buffer_3_out, controlled_buffer_5_out,
       controlled_buffer_7_out;
  wire [31:0] BlockOut;

  Multiplexer #(.enable("false")) multiplexer_1 (.in0(1'b0), .in1(WriteByte), .out(WriteByte_t), .sel(Enable));
  Multiplexer #(.enable("false")) multiplexer_2 (.in0(1'b0), .in1(WriteBlock), .out(WriteBlock_t), .sel(Enable));
  Demultiplexer #(.select(2), .enable("false")) demultiplexer_1 (
    .out0(Byte0), .out1(Byte1), .out2(Byte2), .out3(Byte3), .in(1'b1), .sel(Addr[1:0]));
  Adder #(.width(2)) adder_1 (.a(BlockAge), .b(2'b01), .out(adder_1_out));  // open: cin, cout
  Register #(.width(7)) Tag (.D(Addr[9:3]), .en(WriteBlock_t), .Q(EvictedBlockTag), .clk(Clock));  // open: clr
  // Probe on EvictedBlockTag
  or or_1 (or_1_out, WriteByte_t, WriteBlock_t);
  Comparator #(.width(2), .mode("unsigned")) comparator_1 (
    .a(BlockAge), .b(AgeAccessed), .eq(comparator_1_eq[0]), .lt(comparator_1_eq[1]));  // open: gt
  Comparator #(.width(7), .mode("unsigned")) comparator_2 (
    .a(Addr[9:3]), .b(EvictedBlockTag), .eq(comparator_2_eq));  // open: gt, lt
  S_R_Flip_Flop s_r_ff_1 (.S(WriteByte_t), .clk(Clock), .R(WriteBlock_t), .Q(IsDirty));  // open: Qn, preset, reset, en
  Register #(.width(1)) Valid (.D(1'b1), .en(or_1_out), .Q(IsValid), .clk(Clock));  // open: clr
  Multiplexer #(.select(2), .width(2), .enable("false")) multiplexer_3 (
    .in0(BlockAge), .in1(2'b00), .in2(adder_1_out), .out(multiplexer_3_out), .sel(comparator_1_eq));  // open: in3
  assign controlled_buffer_1_out = WriteByte_t ? ByteToWrite : 8'bz;  // Controlled_Buffer controlled_buffer_1
  assign controlled_buffer_1_out = WriteBlock_t ? BlockToWrite[7:0] : 8'bz;  // Controlled_Buffer controlled_buffer_2
  assign controlled_buffer_3_out = WriteByte_t ? ByteToWrite : 8'bz;  // Controlled_Buffer controlled_buffer_3
  assign controlled_buffer_3_out = WriteBlock_t ? BlockToWrite[15:8] : 8'bz;  // Controlled_Buffer controlled_buffer_4
  assign controlled_buffer_5_out = WriteByte_t ? ByteToWrite : 8'bz;  // Controlled_Buffer controlled_buffer_5
  assign controlled_buffer_5_out = WriteBlock_t ? BlockToWrite[23:16] : 8'bz;  // Controlled_Buffer controlled_buffer_6
  assign controlled_buffer_7_out = WriteByte_t ? ByteToWrite : 8'bz;  // Controlled_Buffer controlled_buffer_7
  assign controlled_buffer_7_out = WriteBlock_t ? BlockToWrite[31:24] : 8'bz;  // Controlled_Buffer controlled_buffer_8
  and and_1 (InBlock, IsValid, comparator_2_eq);
  Multiplexer #(.width(2), .enable("false")) multiplexer_4 (
    .in0(multiplexer_3_out), .in1(StartAge), .out(multiplexer_4_out), .sel(Init));
  Register #(.width(2)) Age (.D(multiplexer_4_out), .en(or_2_out), .Q(BlockAge), .clk(Clock));  // open: clr
  or or_2 (or_2_out, UpdateAge, Init);
  or or_3 (or_3_out, WriteBlock_t, Byte0);
  or or_4 (or_4_out, WriteBlock_t, Byte1);
  or or_5 (or_5_out, WriteBlock_t, Byte2);
  or or_6 (or_6_out, WriteBlock_t, Byte3);
  // Probe on BlockAge
  // Probe on BlockOut[7:0]
  Register V0 (.D(controlled_buffer_1_out), .en(or_3_out), .Q(BlockOut[7:0]), .clk(Clock));  // open: clr
  // Probe on BlockOut[15:8]
  Register V1 (.D(controlled_buffer_3_out), .en(or_4_out), .Q(BlockOut[15:8]), .clk(Clock));  // open: clr
  // Probe on BlockOut[23:16]
  Register V2 (.D(controlled_buffer_5_out), .en(or_5_out), .Q(BlockOut[23:16]), .clk(Clock));  // open: clr
  // Probe on BlockOut[31:24]
  Register V3 (.D(controlled_buffer_7_out), .en(or_6_out), .Q(BlockOut[31:24]), .clk(Clock));  // open: clr
  // Probe on BlockOut
  Multiplexer #(.width(32), .enable("false")) multiplexer_5 (
    .in0({32{1'b0}}), .in1(BlockOut), .out(BlockData), .sel(Enable));

  // Other names for the same wires on the sheet: Index[1:0] = Addr[1:0]; Set = Addr[2]; Tag[6:0] = Addr[9:3];
  //   V0Block[7:0] = BlockToWrite[7:0]; V1Block[7:0] = BlockToWrite[15:8]; V2Block[7:0] = BlockToWrite[23:16];
  //   V3Block[7:0] = BlockToWrite[31:24]; CurrentTag[6:0] = EvictedBlockTag; V0Byte[7:0] = ByteToWrite;
  //   V1Byte[7:0] = ByteToWrite; V2Byte[7:0] = ByteToWrite; V3Byte[7:0] = ByteToWrite
endmodule

module test (
  input  Enable,
  input  UpdateAges,
  input  EvictBlock,
  input  [9:0] Addr,
  input  WriteByte,
  input  [7:0] ByteToWrite,
  input  WriteBlock,
  input  [31:0] BlockToWrite,
  input  Init,
  input  [9:0] Addr_2,
  input  WriteByte_2,
  input  [7:0] ByteToWrite_2,
  input  WriteBlock_2,
  input  [31:0] BlockToWrite_2,
  input  UpdateAge,
  input  [1:0] AgeAccessed
);

  wire clock_1_out, clock_2_out, Dirty, InBlocka, InCache, IsDirtya;
  wire [1:0] BlockAgea;
  wire [7:0] ByteOut;
  wire [31:0] BlockDataa, BlockOut;

  Clock clock_1 (.out(clock_1_out));
  Clock clock_2 (.out(clock_2_out));
  // Set set_1: pin names not known; wires that end beside it: 1'b0, Enable, UpdateAges, EvictBlock, Addr, WriteByte, ByteToWrite, WriteBlock, BlockToWrite, clock_1_out, InCache, Dirty, ByteOut, BlockOut
  // Probe on InCache
  // Probe on BlockOut
  Block2 block2_1 (
    .Enable(1'b1), .Init(Init), .StartAge(2'b10), .Addr(Addr_2), .WriteByte(WriteByte_2),
    .ByteToWrite(ByteToWrite_2), .WriteBlock(WriteBlock_2), .BlockToWrite(BlockToWrite_2),
    .UpdateAge(UpdateAge), .AgeAccessed(AgeAccessed), .Clock(clock_2_out), .InBlock(InBlocka),
    .IsDirty(IsDirtya), .BlockData(BlockDataa), .BlockAge(BlockAgea));  // open: EvictedBlockTag
  // Probe on Dirty
  // Probe on BlockAgea
  // Probe on ByteOut
  // Probe on BlockDataa
endmodule

module Next_State (
  input  S2,
  input  S1,
  input  S0,
  input  C,
  input  R,
  input  W,
  input  D,
  output S2P,
  output S1P,
  output S0P
);

  wire and_1_out, and_2_out, and_3_out, and_4_out, and_5_out, and_6_out, and_7_out, and_8_out, and_9_out,
       not_1_out, not_2_out, not_3_out, not_4_out, not_5_out, not_6_out, not_7_out, not_8_out, not_9_out,
       not_10_out, not_11_out;

  not not_1 (not_1_out, S0);
  not not_2 (not_2_out, S0);
  not not_3 (not_3_out, C);
  not not_4 (not_4_out, S0);
  not not_5 (not_5_out, S2);
  not not_6 (not_6_out, S0);
  not not_7 (not_7_out, S0);
  not not_8 (not_8_out, S1);
  not not_9 (not_9_out, S0);
  not not_10 (not_10_out, D);
  not not_11 (not_11_out, R);
  and and_1 (and_1_out, S1, not_1_out, W);
  and and_2 (and_2_out, S1, not_2_out, R);
  and and_3 (and_3_out, S2, not_3_out);
  and and_4 (and_4_out, S2, S1, not_4_out);
  or or_1 (S1P, not_5_out, S0);
  and and_5 (and_5_out, S1, not_6_out, C, W);
  and and_6 (and_6_out, S1, not_7_out, C, R);
  and and_7 (and_7_out, S2, not_8_out);
  and and_8 (and_8_out, S2, not_9_out, not_10_out);
  and and_9 (and_9_out, S2, C, not_11_out);
  or or_2 (S2P, and_1_out, and_2_out, and_3_out, and_4_out);
  or or_3 (S0P, and_5_out, and_6_out, and_7_out, and_8_out, and_9_out);
endmodule

module OutputEquation (
  input  S2,
  input  S1,
  input  S0,
  input  Clock,
  input  S2_2,
  input  S1_2,
  input  S0_2,
  output MemRead,
  output MemWrite,
  output Evict,
  output UpdateAge,
  output WriteBlock,
  output WriteByte,
  output Init,
  output Ready,
  output InCache
);

  wire and_1_out, and_2_out, and_3_out, and_4_out, and_5_out, and_6_out, and_7_out, and_8_out, and_9_out,
       or_1_out;

  and and_1 (and_1_out, S2_2, S1_2, ~S0_2);  // AND_Gate
  and and_2 (and_2_out, ~S2, S1, ~S0);  // AND_Gate
  and and_3 (and_3_out, ~S2, S1, ~S0);  // AND_Gate
  and and_4 (and_4_out, S2_2, S1_2, S0_2);
  and and_5 (and_5_out, and_1_out, and_2_out);
  and and_6 (and_6_out, S2_2, S1_2, S0_2);
  or or_1 (or_1_out, and_5_out, and_7_out);
  and and_7 (and_7_out, and_3_out, and_4_out);
  and and_8 (and_8_out, S2, ~S0);  // AND_Gate
  and and_9 (and_9_out, S2, ~S1);  // AND_Gate
  and and_10 (MemRead, S0, ~S1);  // AND_Gate
  and and_11 (MemWrite, S2, ~S1, ~S0);  // AND_Gate
  or or_2 (Evict, and_8_out, and_9_out);
  and and_12 (Init, ~S2, ~S1);  // AND_Gate
  and and_13 (Ready, ~S2, S1, ~S0);  // AND_Gate
  Register #(.width(1)) State (.D(and_6_out), .en(or_1_out), .Q(InCache), .clk(Clock));  // open: clr
  and and_14 (UpdateAge, S2, S1, S0);
  and and_15 (WriteBlock, ~S1, S0);  // AND_Gate
  and and_16 (WriteByte, S0, ~S2);  // AND_Gate

  // Other names for the same wires on the sheet: ReadMem = MemRead; S0Next = S0_2; S1Next = S1_2; S2Next = S2_2
endmodule
